// Logisim project preob.circ as structural Verilog: 1 circuit, main circuit main
module main (
  input  x1,
  input  x2,
  input  x3,
  input  x4,
  output out_5,
  output out_6,
  output out_7,
  output out_8
);

  wire and_1_out, and_2_out, and_3_out, and_4_out, and_5_out, and_6_out, and_7_out, not_1_out, not_2_out,
       not_3_out, not_4_out;

  not not_1 (not_1_out, x1);
  not not_2 (not_2_out, x2);
  not not_3 (not_3_out, x3);
  not not_4 (not_4_out, x4);
  and and_1 (and_1_out, x1, x2, not_3_out);
  and and_2 (and_2_out, not_1_out, not_2_out, x3);
  and and_3 (and_3_out, not_2_out, not_3_out);
  and and_4 (and_4_out, x1, not_2_out);
  and and_5 (and_5_out, not_1_out, not_2_out, not_3_out);
  and and_6 (and_6_out, x1, not_2_out, x3);
  and and_7 (and_7_out, not_1_out, x2, x3);
  or or_1 (out_5, and_1_out, and_2_out);
  or or_2 (out_6, and_3_out, and_4_out);
  or or_3 (out_7, and_5_out, and_6_out, and_7_out);

  assign out_8 = x4;

  // Notes on the sheet:
  //   !x1
  //   !x2
  //   !x3
  //   !x4
  //   x1
  //   x2
  //   x3
  //   x4
  //   !x1
  //   !x2
  //   !x3
  //   !x4
endmodule
