// Logisim project summator.circ as structural Verilog: 1 circuit, main circuit main
module main (
  input  [7:0] in_1,
  input  x1,
  input  in_3,
  input  x2,
  input  [7:0] in_5,
  input  x3,
  output [7:0] out_7,
  output [7:0] out_8,
  output S,
  output [7:0] out_10,
  output [7:0] out_11,
  output out_12,
  output P
);

  wire and_1_out, and_2_out, and_3_out, and_4_out, and_5_out, and_6_out, and_7_out, and_8_out, and_9_out,
       and_10_out, and_11_out, and_12_out, and_13_out, and_14_out, and_15_out, and_16_out, and_17_out,
       and_18_out, and_19_out, not_1_out, not_2_out, not_3_out, or_2_out, or_3_out, or_4_out, or_5_out,
       or_6_out, or_7_out, or_8_out, xor_1_out, xor_3_out, xor_4_out, xor_5_out, xor_6_out, xor_7_out,
       xor_8_out, xor_9_out, xor_10_out;

  not not_1 (not_1_out, x1);
  not not_2 (not_2_out, x2);
  not not_3 (not_3_out, x3);
  xor xor_1 (xor_1_out, x1, x2);
  xor xor_2 (S, xor_1_out, x3);
  and and_1 (and_1_out, x1, x3);
  and and_2 (and_2_out, x1, x2);
  and and_3 (and_3_out, x2, x3);
  or or_1 (P, and_1_out, and_2_out, and_3_out);
  xor xor_3 (xor_3_out, in_1[0], in_5[0]);
  and and_4 (and_4_out, in_5[0], in_1[0]);
  xor xor_4 (xor_4_out, in_1[1], in_5[1]);
  and and_5 (and_5_out, in_5[1], in_1[1]);
  xor xor_5 (xor_5_out, in_1[2], in_5[2]);
  and and_6 (and_6_out, in_5[2], in_1[2]);
  xor xor_6 (xor_6_out, in_1[3], in_5[3]);
  and and_7 (and_7_out, in_5[3], in_1[3]);
  xor xor_7 (xor_7_out, in_1[4], in_5[4]);
  and and_8 (and_8_out, in_5[4], in_1[4]);
  xor xor_8 (xor_8_out, in_1[5], in_5[5]);
  and and_9 (and_9_out, in_5[5], in_1[5]);
  xor xor_9 (xor_9_out, in_1[6], in_5[6]);
  and and_10 (and_10_out, in_5[6], in_1[6]);
  xor xor_10 (xor_10_out, in_1[7], in_5[7]);
  and and_11 (and_11_out, in_5[7], in_1[7]);
  xor xor_11 (out_8[0], xor_3_out, in_3);
  and and_12 (and_12_out, xor_3_out, in_3);
  and and_13 (and_13_out, xor_4_out, or_2_out);
  and and_14 (and_14_out, xor_5_out, or_3_out);
  and and_15 (and_15_out, xor_6_out, or_4_out);
  and and_16 (and_16_out, xor_7_out, or_5_out);
  and and_17 (and_17_out, xor_8_out, or_6_out);
  and and_18 (and_18_out, xor_9_out, or_7_out);
  and and_19 (and_19_out, xor_10_out, or_8_out);
  or or_2 (or_2_out, and_12_out, and_4_out);
  xor xor_12 (out_8[1], xor_4_out, or_2_out);
  or or_3 (or_3_out, and_13_out, and_5_out);
  xor xor_13 (out_8[2], xor_5_out, or_3_out);
  or or_4 (or_4_out, and_14_out, and_6_out);
  xor xor_14 (out_8[3], xor_6_out, or_4_out);
  or or_5 (or_5_out, and_15_out, and_7_out);
  xor xor_15 (out_8[4], xor_7_out, or_5_out);
  or or_6 (or_6_out, and_16_out, and_8_out);
  xor xor_16 (out_8[5], xor_8_out, or_6_out);
  or or_7 (or_7_out, and_17_out, and_9_out);
  xor xor_17 (out_8[6], xor_9_out, or_7_out);
  or or_8 (or_8_out, and_18_out, and_10_out);
  xor xor_18 (out_8[7], xor_10_out, or_8_out);
  or or_9 (out_12, and_19_out, and_11_out);

  assign out_7 = in_1;
  assign out_10 = out_8;
  assign out_11 = in_5;

  // Notes on the sheet:
  //   !x1
  //   !x2
  //   !x3
  //   x1
  //   x2
  //   x3
  //   !x1
  //   !x2
  //   !x3
  //   x1
  //   x3
  //   x1
  //   x2
  //   x2
  //   x3
endmodule
