// Logisim project TriggerT.circ as structural Verilog: 1 circuit, main circuit main
module main (
  input  in_1,
  input  in_2,
  input  S,
  input  in_4,
  input  x1,
  input  S_2,
  input  x2,
  input  in_8,
  input  R,
  input  x3,
  input  in_11,
  input  R_2,
  input  x4,
  input  in_14,
  input  in_15,
  input  S_3,
  input  in_17,
  input  in_18,
  input  in_19,
  input  R_3,
  output nQ,
  output out_22,
  output out_23,
  output out_24,
  output nQ_2,
  output out_26,
  output Q,
  output Q_2,
  output nQ_3,
  output out_30,
  output Q_3,
  output out_32,
  output out_33,
  output [3:0] out_34,
  output Q_4,
  output nQ_4,
  output out_37,
  output out_38
);

  wire and_1_out, and_2_out, and_3_out, and_4_out, and_5_out, and_6_out, and_7_out, and_8_out, and_9_out,
       and_10_out, and_11_out, and_12_out, and_13_out, and_14_out, nand_1_out, nand_2_out, nand_7_out,
       nand_8_out, nand_9_out, nand_10_out, nand_11_out, nand_12_out, nand_13_out, nand_14_out, nand_15_out,
       nand_16_out, nand_17_out, nand_18_out, nand_19_out, nand_20_out, nand_21_out, nand_22_out,
       nand_23_out, nand_24_out, nand_26_out, nand_28_out, nand_30_out, nand_31_out, nand_32_out,
       nand_33_out, nand_34_out, nand_35_out, nand_36_out, nand_38_out, nand_39_out, nand_40_out,
       nand_41_out, nand_42_out, nand_43_out, nand_44_out, nand_45_out, nand_46_out, nand_47_out,
       nand_48_out, nand_49_out, nand_50_out, nand_51_out, nand_52_out, nand_53_out, nand_54_out,
       nand_55_out, nand_56_out, nand_57_out, nand_59_out, nand_61_out, not_3_out, not_4_out, not_5_out,
       not_7_out, not_8_out, not_9_out;

  not not_1 (out_22, in_4);
  not not_2 (in_4, out_22);
  nand nand_1 (nand_1_out, nQ_4, S_3, in_18);
  nand nand_2 (nand_2_out, in_18, R_3, Q_4);
  nand nand_3 (Q_4, nand_1_out, nQ_4);
  nand nand_4 (nQ_4, Q_4, nand_2_out);
  nand nand_5 (nQ, S, Q);
  nor nor_1 (nQ_3, in_11, Q_3);
  nand nand_6 (Q, nQ, R);
  nor nor_2 (Q_3, nQ_3, in_15);
  nand nand_7 (nand_7_out, nand_26_out, in_17, in_19);
  nand nand_8 (nand_8_out, in_19, in_17, out_34[0]);
  nand nand_9 (nand_9_out, nand_28_out, out_34[0], in_19);
  nand nand_10 (nand_10_out, in_19, out_34[0], out_34[1]);
  nand nand_11 (nand_11_out, nand_30_out, and_3_out, in_19);
  nand nand_12 (nand_12_out, in_19, and_3_out, out_34[2]);
  nand nand_13 (nand_13_out, nand_7_out, nand_14_out);
  nand nand_14 (nand_14_out, nand_13_out, nand_8_out);
  nand nand_15 (nand_15_out, nand_9_out, nand_16_out);
  nand nand_16 (nand_16_out, nand_15_out, nand_10_out);
  nand nand_17 (nand_17_out, nand_11_out, nand_18_out);
  nand nand_18 (nand_18_out, nand_17_out, nand_12_out);
  nand nand_19 (nand_19_out, nand_7_out, nand_13_out);
  nand nand_20 (nand_20_out, nand_14_out, nand_8_out);
  nand nand_21 (nand_21_out, nand_9_out, nand_15_out);
  nand nand_22 (nand_22_out, nand_16_out, nand_10_out);
  nand nand_23 (nand_23_out, nand_11_out, nand_17_out);
  nand nand_24 (nand_24_out, nand_18_out, nand_12_out);
  and and_1 (and_1_out, S_2, in_8);
  and and_2 (and_2_out, in_8, R_2);
  nand nand_25 (out_34[0], nand_19_out, nand_26_out);
  nand nand_26 (nand_26_out, out_34[0], nand_20_out);
  nand nand_27 (out_34[1], nand_21_out, nand_28_out);
  nand nand_28 (nand_28_out, out_34[1], nand_22_out);
  nand nand_29 (out_34[2], nand_23_out, nand_30_out);
  nand nand_30 (nand_30_out, out_34[2], nand_24_out);
  nor nor_3 (nQ_2, and_1_out, Q_2);
  nor nor_4 (Q_2, nQ_2, and_2_out);
  and and_3 (and_3_out, out_34[0], out_34[1]);
  and and_4 (and_4_out, out_34[0], out_34[1], out_34[2]);
  nand nand_31 (nand_31_out, nand_38_out, and_4_out, in_19);
  nand nand_32 (nand_32_out, in_19, and_4_out, out_34[3]);
  nand nand_33 (nand_33_out, nand_31_out, nand_34_out);
  nand nand_34 (nand_34_out, nand_33_out, nand_32_out);
  nand nand_35 (nand_35_out, nand_31_out, nand_33_out);
  nand nand_36 (nand_36_out, nand_34_out, nand_32_out);
  nand nand_37 (out_34[3], nand_35_out, nand_38_out);
  nand nand_38 (nand_38_out, out_34[3], nand_36_out);
  not not_3 (not_3_out, x1);
  not not_4 (not_4_out, x2);
  not not_5 (not_5_out, x3);
  not not_6 (out_37, x4);
  and and_5 (and_5_out, x1, not_4_out);
  and and_6 (and_6_out, not_5_out, x2);
  and and_7 (and_7_out, x1, out_37);
  and and_8 (and_8_out, not_3_out, x2, x3, x4);
  and and_9 (and_9_out, x2, not_5_out);
  and and_10 (and_10_out, x4, x3, not_4_out);
  and and_11 (and_11_out, x2, out_37);
  and and_12 (and_12_out, not_5_out, x4);
  and and_13 (and_13_out, x3, out_37);
  or or_1 (out_23, and_5_out, and_6_out, and_7_out, and_8_out);
  or or_2 (out_30, and_9_out, and_10_out, and_11_out);
  or or_3 (out_33, and_12_out, and_13_out);
  nand nand_39 (nand_39_out, out_26, in_2, in_14);
  nand nand_40 (nand_40_out, in_14, in_2, nand_57_out);
  nand nand_41 (nand_41_out, out_32, not_7_out, in_14);
  nand nand_42 (nand_42_out, in_14, not_7_out, nand_59_out);
  nand nand_43 (nand_43_out, out_38, and_14_out, in_14);
  nand nand_44 (nand_44_out, in_14, and_14_out, nand_61_out);
  nand nand_45 (nand_45_out, nand_39_out, nand_46_out);
  nand nand_46 (nand_46_out, nand_45_out, nand_40_out);
  nand nand_47 (nand_47_out, nand_41_out, nand_48_out);
  nand nand_48 (nand_48_out, nand_47_out, nand_42_out);
  nand nand_49 (nand_49_out, nand_43_out, nand_50_out);
  nand nand_50 (nand_50_out, nand_49_out, nand_44_out);
  nand nand_51 (nand_51_out, nand_39_out, nand_45_out);
  nand nand_52 (nand_52_out, nand_46_out, nand_40_out);
  not not_7 (not_7_out, out_26);
  nand nand_53 (nand_53_out, nand_41_out, nand_47_out);
  nand nand_54 (nand_54_out, nand_48_out, nand_42_out);
  nand nand_55 (nand_55_out, nand_43_out, nand_49_out);
  nand nand_56 (nand_56_out, nand_50_out, nand_44_out);
  nand nand_57 (nand_57_out, nand_51_out, out_26);
  nand nand_58 (out_26, nand_57_out, nand_52_out);
  nand nand_59 (nand_59_out, nand_53_out, out_32);
  nand nand_60 (out_32, nand_59_out, nand_54_out);
  nand nand_61 (nand_61_out, nand_55_out, out_38);
  nand nand_62 (out_38, nand_61_out, nand_56_out);
  not not_8 (not_8_out, out_26);
  not not_9 (not_9_out, out_32);
  and and_14 (and_14_out, not_8_out, not_9_out);

  assign out_24 = in_4;

  // Notes on the sheet:
  //   Бит синхронизации
  //   Простой flip-flop
  //   Синхронный JK-триггер
  //   RS-триггер
  //   Многоуровневый Синхронный JK-триггер
  //   Бит синхронизации
  //   Синхронный RS-триггер
  //   !x1
  //   !x2
  //   !x3
  //   !x4
  //   x1
  //   x2
  //   x3
  //   x4
  //   !x1
  //   !x2
  //   !x3
  //   !x4
endmodule
